// Logisim project half adder.circ as structural Verilog: 1 circuit, main circuit main
module main (
  input  a,
  input  b,
  output s,
  output c
);

  xor xor_1 (s, a, b);
  and and_1 (c, a, b);
endmodule
